# Fritzing sketch FritzSchematic (saved by Fritzing 0.9.3b)

parts:
  Raspberry_Pi1 = Raspberry Pi B+
  R1 = Photocell (LDR) [package=THT]
  C1 = Electrolytic Capacitor [capacitance=1000μF package="1010 [SMD, electrolytic]"]
  LED1 = Gus the Green LED
  LED2 = Gus the Green LED
  LED3 = Gus the Green LED
  LED4 = Gus the Green LED
  R2 = Resistor [tolerance=±5% resistance=220 package="2512 [SMD]"]
  SERVO1 = Adafruit Feedback Servo (small)

nets:
  N1: Raspberry_Pi1.GPIO4, R1.pin_0, C1.+
  N2: Raspberry_Pi1.GND, C1.-, LED1.cathode, LED2.cathode, LED3.cathode, LED4.cathode, SERVO1.Ground
  N3: Raspberry_Pi1.GPIO26, R2.Pin_1
  N4: Raspberry_Pi1.GPIO18, SERVO1.Signal
  N5: Raspberry_Pi1.5V, R1.pin_1, SERVO1.Power
  N6: LED1.anode, LED2.anode, LED3.anode, LED4.anode, R2.Pin_0

custom parts:
  Adafruit Feedback Servo (small): Adafruit Feedback Servo (Small)
